// Logisim project alu.circ as structural Verilog: 15 circuits, main circuit alu
module alu (
  input  [31:0] A,
  input  [31:0] B,
  input  [3:0] ALUSel,
  output [31:0] Result
);


  // Notes on the sheet:
  //   INPUTS to your circuit
  //   DON'T CHANGE THE LOCATIONS OF THE INPUTS AND OUTPUTS!
  //   OUTPUT from your circuit
endmodule

module add_result (
  input  [31:0] A,
  input  [31:0] B,
  output [31:0] Result
);

  Adder #(.width(32)) adder_1 (.a(A), .b(B), .out(Result));  // open: cin, cout
endmodule

module sub_result (
  input  [31:0] A,
  input  [31:0] B,
  output [31:0] Result
);

  Subtractor #(.width(32)) subtractor_1 (.a(A), .b(B), .out(Result));  // open: bin, bout
endmodule

module and_result (
  input  [31:0] A,
  input  [31:0] B,
  output [31:0] Result
);

  assign Result = A & B;  // AND_Gate and_1, 32 bits wide
endmodule

module or_result (
  input  [31:0] A,
  input  [31:0] B,
  output [31:0] result
);

  assign result = A | B;  // OR_Gate or_1, 32 bits wide
endmodule

module xor_result (
  input  [31:0] A,
  input  [31:0] B,
  output [31:0] Result
);

  assign Result = A ^ B;  // XOR_Gate xor_1, 32 bits wide
endmodule

module srl_result (
  input  [31:0] A,
  input  [31:0] B,
  output [31:0] Result
);

  Shifter #(.width(32), .shift("lr")) shifter_1 (.in(A), .\dist (B[4:0]), .out(Result));
endmodule

module sra_result (
  input  [31:0] A,
  input  [31:0] B,
  output [31:0] Result
);

  Shifter #(.width(32), .shift("ar")) shifter_1 (.in(A), .\dist (B[4:0]), .out(Result));
endmodule

module slt_result (
  input  [31:0] A,
  input  [31:0] B,
  output [31:0] Result
);

  wire comparator_1_lt;

  Comparator #(.width(32)) comparator_1 (.a(A), .b(B), .lt(comparator_1_lt));  // open: gt, eq
  Multiplexer #(.width(32), .enable("false")) multiplexer_1 (
    .in0({32{1'b0}}), .in1(32'h1), .out(Result), .sel(comparator_1_lt));
endmodule

module cnto_result (
  input  [31:0] A,
  input  [31:0] B,
  output [31:0] Result
);

  BitAdder #(.width(32)) bitadder_1 (.in0(A), .in1(B), .out(Result[6:0]));

  assign Result[31:7] = {25{1'b0}};
endmodule

module sir_result (
  input  [31:0] A,
  input  [31:0] B,
  output [31:0] Result
);

  wire comparator_1_eq;

  Comparator #(.width(32)) comparator_1 (
    .a(A),
    .b({B[0], B[1], B[2], B[3], B[4], B[5], B[6], B[7], B[8], B[9], B[10], B[11], B[12], B[13], B[14], B[15], B[16], B[17], B[18], B[19], B[20], B[21], B[22], B[23], B[24], B[25], B[26], B[27], B[28], B[29], B[30], B[31]}),
    .eq(comparator_1_eq));  // open: gt, lt
  assign Result = {{31{1'b0}}, comparator_1_eq};  // Bit_Extender bit_extender_1
endmodule

module mult_result (
  input  [31:0] A,
  input  [31:0] B,
  output [31:0] Result,
  output [31:0] out_4
);

  Multiplier #(.width(32)) multiplier_1 (.a(A), .b(B), .out(Result), .cout(out_4));  // open: cin
endmodule

module divu_result (
  input  [31:0] A,
  input  [31:0] B,
  output [31:0] Result
);

  Divider #(.width(32)) divider_1 (.a(A), .b(B), .out(Result));  // open: upper, rem
endmodule

module div_result (
  input  [31:0] A,
  input  [31:0] B,
  output [31:0] Result
);

  wire Sign_bit;
  wire [31:0] divider_1_out, multiplexer_1_out, multiplexer_2_out, negator_1_out, negator_2_out,
       negator_3_out;

  Negator #(.width(32)) negator_1 (.in(A), .out(negator_1_out));
  Negator #(.width(32)) negator_2 (.in(B), .out(negator_2_out));
  Multiplexer #(.width(32), .enable("false")) multiplexer_1 (
    .in0(A), .in1(negator_1_out), .out(multiplexer_1_out), .sel(A[31]));
  xor xor_1 (Sign_bit, A[31], B[31]);
  Multiplexer #(.width(32), .enable("false")) multiplexer_2 (
    .in0(B), .in1(negator_2_out), .out(multiplexer_2_out), .sel(B[31]));
  Divider #(.width(32)) divider_1 (
    .a(multiplexer_1_out), .b(multiplexer_2_out), .out(divider_1_out));  // open: upper, rem
  Negator #(.width(32)) negator_3 (.in(divider_1_out), .out(negator_3_out));
  Multiplexer #(.width(32), .enable("false")) multiplexer_3 (
    .in0(divider_1_out), .in1(negator_3_out), .out(Result), .sel(Sign_bit));
endmodule

module remu_result (
  input  [31:0] A,
  input  [31:0] B,
  output [31:0] Result
);

  Divider #(.width(32)) divider_1 (.a(A), .b(B), .rem(Result));  // open: out, upper
endmodule
