// Logisim project regfile.circ as structural Verilog: 2 circuits, main circuit main
module main (
  input  [4:0] rs1,
  input  [4:0] rs2,
  input  [4:0] rd,
  input  [31:0] Write_Data,
  input  RegWEn,
  input  clk,
  output [31:0] ra,
  output [31:0] sp,
  output [31:0] t0,
  output [31:0] t1,
  output [31:0] t2,
  output [31:0] s0,
  output [31:0] s1,
  output [31:0] a0,
  output [31:0] Read_Data_1,
  output [31:0] Read_Data_2,
  output [3:0] out_17
);

  wire en1, en2, en5, en6, en7, en8, en9, en10;
  wire [31:0] selector_1_result, selector_2_result, selector_3_result, selector_4_result, selector_5_result,
       selector_6_result, selector_7_result, selector_8_result, zero;

  Demultiplexer #(.select(4), .enable("false")) demultiplexer_1 (
    .out1(en1), .out2(en2), .out5(en5), .out6(en6), .out7(en7), .out8(en8), .out9(en9), .out10(en10),
    .in(RegWEn), .sel(rd[3:0]));  // open: out0, out3, out4, out11, out12, out13, out14, out15
  Register #(.width(32)) x0 (.clk(clk), .Q(zero), .clr(1'b1));  // open: D, en
  Register #(.width(32)) x5 (.D(selector_1_result), .clk(clk), .Q(t0));  // open: en, clr
  Register #(.width(32)) x8 (.D(selector_2_result), .clk(clk), .Q(s0));  // open: en, clr
  selector selector_1 (.Write_data(Write_Data), .en(en5), .self(t0), .Result(selector_1_result));
  selector selector_2 (.Write_data(Write_Data), .en(en8), .self(s0), .Result(selector_2_result));
  Register #(.width(32)) x1 (.D(selector_3_result), .clk(clk), .Q(ra));  // open: en, clr
  Register #(.width(32)) x6 (.D(selector_4_result), .clk(clk), .Q(t1));  // open: en, clr
  Register #(.width(32)) x9 (.D(selector_5_result), .clk(clk), .Q(s1));  // open: en, clr
  selector selector_3 (.Write_data(Write_Data), .en(en1), .self(ra), .Result(selector_3_result));
  selector selector_4 (.Write_data(Write_Data), .en(en6), .self(t1), .Result(selector_4_result));
  selector selector_5 (.Write_data(Write_Data), .en(en9), .self(s1), .Result(selector_5_result));
  Multiplexer #(.select(4), .width(32), .enable("false")) multiplexer_1 (
    .in0(zero), .in1(ra), .in2(sp), .in5(t0), .in6(t1), .in7(t2), .in8(s0), .in9(s1), .in10(a0),
    .out(Read_Data_1), .sel(rs1[3:0]));  // open: in3, in4, in11, in12, in13, in14, in15
  Multiplexer #(.select(4), .width(32), .enable("false")) multiplexer_2 (
    .in0(zero), .in1(ra), .in2(sp), .in5(t0), .in6(t1), .in7(t2), .in8(s0), .in9(s1), .in10(a0),
    .out(Read_Data_2), .sel(rs2[3:0]));  // open: in3, in4, in11, in12, in13, in14, in15
  Register #(.width(32)) x2 (.D(selector_6_result), .clk(clk), .Q(sp));  // open: en, clr
  Register #(.width(32)) x7 (.D(selector_7_result), .clk(clk), .Q(t2));  // open: en, clr
  Register #(.width(32)) x10 (.D(selector_8_result), .clk(clk), .Q(a0));  // open: en, clr
  selector selector_6 (.Write_data(Write_Data), .en(en2), .self(sp), .Result(selector_6_result));
  selector selector_7 (.Write_data(Write_Data), .en(en7), .self(t2), .Result(selector_7_result));
  selector selector_8 (.Write_data(Write_Data), .en(en10), .self(a0), .Result(selector_8_result));

  assign out_17 = rs1[3:0];

  // Other names for the same wires on the sheet: read_data1[31:0] = Read_Data_1; read_data2[31:0] = Read_Data_2;
  //   read_reg1[4:0] = rs1; read_reg2[4:0] = rs2; write_en = RegWEn; write_reg[4:0] = rd

  // Notes on the sheet:
  //   INPUTS to your circuit
  //   DON'T CHANGE THE LOCATIONS OF THE INPUTS AND OUTPUTS!
  //   These are DEBUG/TEST outputs from your circuit.
  //   OUTPUTS from your circuit
endmodule

module selector (
  input  en,
  input  [31:0] self,
  input  [31:0] Write_data,
  output [31:0] Result
);

  Multiplexer #(.width(32), .enable("false")) multiplexer_1 (.in0(self), .in1(Write_data), .out(Result), .sel(en));
endmodule
