// Logisim project alu.circ as structural Verilog: 19 circuits, main circuit and_result
module alu (
  input  [31:0] A,
  input  [31:0] B,
  input  [3:0] ALUSel,
  output [31:0] Result
);

  wire [31:0] result0, result1, result2, result3, result4, result5, result6, result7, result8, result9,
       result10, result11, result12, result13, result14, result15;

  B_result b_result_1 (.A(A), .B(B), .Result(result10));
  add_result add_result_1 (.A(A), .B(B), .Result(result0));
  sll_result sll_result_1 (.A(A), .B(B), .Result(result1));
  slt_result slt_result_1 (.A(A), .B(B), .Result(result2));
  sub_result sub_result_1 (.A(A), .B(B), .Result(result3));
  divu_result divu_result_1 (.A(A), .B(B), .Result(result13));
  xor_result xor_result_1 (.A(A), .B(B), .Result(result4));
  srl_result srl_result_1 (.A(A), .B(B), .Result(result5));
  or_result or_result_1 (.A(A), .B(B), .result(result6));
  and_result and_result_1 (.A(A), .B(B), .Result(result7));
  remu_result remu_result_1 (.A(A), .B(B), .Result(result15));
  Multiplexer #(.select(4), .width(32), .enable("false")) multiplexer_1 (
    .in0(result0), .in1(result1), .in2(result2), .in3(result3), .in4(result4), .in5(result5), .in6(result6),
    .in7(result7), .in8(result8), .in9(result9), .in10(result10), .in11(result11), .in12(result12),
    .in13(result13), .in14(result14), .in15(result15), .out(Result), .sel(ALUSel));
  mult_result mult_result_1 (.A(A), .B(B), .Result(result8));
  mulh_result mulh_result_1 (.A(A), .B(B), .Result(result9));
  mulhu_result mulhu_result_1 (.A(A), .B(B), .Result(result11));
  div_result div_result_1 (.A(A), .B(B), .Result(result12));

  // Notes on the sheet:
  //   INPUTS to your circuit
  //   DON'T CHANGE THE LOCATIONS OF THE INPUTS AND OUTPUTS!
  //   OUTPUT from your circuit
endmodule

module add_result (
  input  [31:0] A,
  input  [31:0] B,
  output [31:0] Result
);

  Adder #(.width(32)) adder_1 (.a(A), .b(B), .out(Result));  // open: cin, cout
endmodule

module sll_result (
  input  [31:0] A,
  input  [31:0] B,
  output [31:0] Result
);

  Shifter #(.width(32)) shifter_1 (.in(A), .\dist (B[4:0]), .out(Result));
endmodule

module slt_result (
  input  [31:0] A,
  input  [31:0] B,
  output [31:0] Result
);

  wire comparator_1_lt;

  Comparator #(.width(32)) comparator_1 (.a(A), .b(B), .lt(comparator_1_lt));  // open: gt, eq
  Multiplexer #(.width(32), .enable("false")) multiplexer_1 (
    .in0({32{1'b0}}), .in1(32'h1), .out(Result), .sel(comparator_1_lt));
endmodule

module sub_result (
  input  [31:0] A,
  input  [31:0] B,
  output [31:0] Result
);

  Subtractor #(.width(32)) subtractor_1 (.a(A), .b(B), .out(Result));  // open: bin, bout
endmodule

module xor_result (
  input  [31:0] A,
  input  [31:0] B,
  output [31:0] Result
);

  assign Result = A ^ B;  // XOR_Gate xor_1, 32 bits wide
endmodule

module srl_result (
  input  [31:0] A,
  input  [31:0] B,
  output [31:0] Result
);

  Shifter #(.width(32), .shift("lr")) shifter_1 (.in(A), .\dist (B[4:0]), .out(Result));
endmodule

module or_result (
  input  [31:0] A,
  input  [31:0] B,
  output [31:0] result
);

  assign result = A | B;  // OR_Gate or_1, 32 bits wide
endmodule

module and_result (
  input  [31:0] A,
  input  [31:0] B,
  output [31:0] Result
);

  assign Result = A & B;  // AND_Gate and_1, 32 bits wide
endmodule

module mult_result (
  input  [31:0] A,
  input  [31:0] B,
  output [31:0] Result
);

  Multiplier #(.width(32)) multiplier_1 (.a(A), .b(B), .out(Result));  // open: cin, cout
endmodule

module mulh_result (
  input  [31:0] A,
  input  [31:0] B,
  output [31:0] Result
);

  wire Sign_bit;
  wire [31:0] multiplexer_1_out, multiplexer_2_out, multiplier_1_cout, negator_1_out, negator_2_out,
       negator_3_out, subtractor_1_out;

  Negator #(.width(32)) negator_1 (.in(A), .out(negator_1_out));
  Negator #(.width(32)) negator_2 (.in(B), .out(negator_2_out));
  Multiplexer #(.width(32), .enable("false")) multiplexer_1 (
    .in0(A), .in1(negator_1_out), .out(multiplexer_1_out), .sel(A[31]));
  xor xor_1 (Sign_bit, A[31], B[31]);
  Multiplexer #(.width(32), .enable("false")) multiplexer_2 (
    .in0(B), .in1(negator_2_out), .out(multiplexer_2_out), .sel(B[31]));
  Multiplier #(.width(32)) multiplier_1 (
    .a(multiplexer_1_out), .b(multiplexer_2_out), .cout(multiplier_1_cout));  // open: out, cin
  Negator #(.width(32)) negator_3 (.in(multiplier_1_cout), .out(negator_3_out));
  Subtractor #(.width(32)) subtractor_1 (.a(negator_3_out), .b(32'h1), .out(subtractor_1_out));  // open: bin, bout
  Multiplexer #(.width(32), .enable("false")) multiplexer_3 (
    .in0(multiplier_1_cout), .in1(subtractor_1_out), .out(Result), .sel(Sign_bit));
endmodule

module B_result (
  input  [31:0] A,
  input  [31:0] B,
  output [31:0] Result
);


  assign Result = B;
endmodule

module mulhu_result (
  input  [31:0] A,
  input  [31:0] B,
  output [31:0] Result
);

  Multiplier #(.width(32)) multiplier_1 (.a(A), .b(B), .cout(Result));  // open: out, cin
endmodule

module div_result (
  input  [31:0] A,
  input  [31:0] B,
  output [31:0] Result
);

  wire Sign_bit;
  wire [31:0] divider_1_out, multiplexer_1_out, multiplexer_2_out, negator_1_out, negator_2_out,
       negator_3_out;

  Negator #(.width(32)) negator_1 (.in(A), .out(negator_1_out));
  Negator #(.width(32)) negator_2 (.in(B), .out(negator_2_out));
  Multiplexer #(.width(32), .enable("false")) multiplexer_1 (
    .in0(A), .in1(negator_1_out), .out(multiplexer_1_out), .sel(A[31]));
  xor xor_1 (Sign_bit, A[31], B[31]);
  Multiplexer #(.width(32), .enable("false")) multiplexer_2 (
    .in0(B), .in1(negator_2_out), .out(multiplexer_2_out), .sel(B[31]));
  Divider #(.width(32)) divider_1 (
    .a(multiplexer_1_out), .b(multiplexer_2_out), .out(divider_1_out));  // open: upper, rem
  Negator #(.width(32)) negator_3 (.in(divider_1_out), .out(negator_3_out));
  Multiplexer #(.width(32), .enable("false")) multiplexer_3 (
    .in0(divider_1_out), .in1(negator_3_out), .out(Result), .sel(Sign_bit));
endmodule

module divu_result (
  input  [31:0] A,
  input  [31:0] B,
  output [31:0] Result
);

  Divider #(.width(32)) divider_1 (.a(A), .b(B), .out(Result));  // open: upper, rem
endmodule

module remu_result (
  input  [31:0] A,
  input  [31:0] B,
  output [31:0] Result
);

  Divider #(.width(32)) divider_1 (.a(A), .b(B), .rem(Result));  // open: out, upper
endmodule

module sra_result (
  input  [31:0] A,
  input  [31:0] B,
  output [31:0] Result
);

  Shifter #(.width(32), .shift("ar")) shifter_1 (.in(A), .\dist (B[4:0]), .out(Result));
endmodule

module sir_result (
  input  [31:0] A,
  input  [31:0] B,
  output [31:0] Result
);

  wire comparator_1_eq;

  Comparator #(.width(32)) comparator_1 (
    .a(A),
    .b({B[0], B[1], B[2], B[3], B[4], B[5], B[6], B[7], B[8], B[9], B[10], B[11], B[12], B[13], B[14], B[15], B[16], B[17], B[18], B[19], B[20], B[21], B[22], B[23], B[24], B[25], B[26], B[27], B[28], B[29], B[30], B[31]}),
    .eq(comparator_1_eq));  // open: gt, lt
  assign Result = {{31{1'b0}}, comparator_1_eq};  // Bit_Extender bit_extender_1
endmodule

module cnto_result (
  input  [31:0] A,
  input  [31:0] B,
  output [31:0] Result
);

  BitAdder #(.width(32)) bitadder_1 (.in0(A), .in1(B), .out(Result[6:0]));

  assign Result[31:7] = {25{1'b0}};
endmodule
